# Fritzing sketch Arduino_ESP8266_five_buttons_NeoPixel (saved by Fritzing 0.9.3b)
perfboards: 1

parts:
  Part1 = Adafruit Feather HUZZAH ESP8266 [part_number="Adafruit #2821"]
  S1 = Momentary Switch [package=ksa_sealed_tac_switch]
  R1 = Resistor [tolerance=±5% resistance=10k package=THT]
  S2 = Momentary Switch [package=ksa_sealed_tac_switch]
  S3 = Momentary Switch [package=ksa_sealed_tac_switch]
  S4 = Momentary Switch [package=ksa_sealed_tac_switch]
  S5 = Momentary Switch [package=ksa_sealed_tac_switch]
  R3 = Resistor [tolerance=±5% resistance=10k package=THT]
  R4 = Resistor [tolerance=±5% resistance=10k package=THT]
  R5 = Resistor [tolerance=±5% resistance=10k package=THT]
  R6 = Resistor [tolerance=±5% resistance=22k package=THT]
  NEOPIXEL3 = Neopixel Strip -- White (60/m) [part_number=1138]
  R7 = Resistor [tolerance=±5% resistance=10k package=THT]

nets:
  N1: Part1.ADC, S1.1
  GND: Part1.GND, Part1.RESET, R1.Pin_0, NEOPIXEL3.GND
  3.3V: Part1.3.3V, R6.Pin_1, NEOPIXEL3.+5V
  N2: Part1.GPIO15, NEOPIXEL3.DI
  N3: S1.2, R1.Pin_1, S2.2, S3.2, S4.2, S5.2
  N4: S1.3, R7.Pin_0
  N5: S5.3, R5.Pin_1, R6.Pin_0
  N6: R3.Pin_0, R7.Pin_1
  N7: R3.Pin_1, R4.Pin_0
  N8: R4.Pin_1, R5.Pin_0

custom parts:
  Adafruit Feather HUZZAH ESP8266: his is the Adafruit Feather HUZZAH ESP8266 - our take on an 'all-in-one' ESP8266 WiFi development board with built in USB and battery charging. Its an ESP8266 WiFi module with all the extras you need, ready to rock! We have other boards in the Feather family, check'em out here. At the Feather HUZZAH's heart is an ESP8266 WiFi microcontroller clocked at 80 MHz and at 3.3V logic. This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
  Neopixel Strip -- White (60/m): Neopixel Strip, White, 60 pixels per meter.
